# Fritzing sketch Circuito (saved by Fritzing 0.9.6b)

parts:
  Componente1 = NRF24L01
  Componente2 = Arduino Uno (Rev3)
  HC-SR04_Sensor_1 = HC-SR04 Ultrasonic Distance Sensor
  J1 = Piezo Speaker
  Componente3 = Arduino Uno (Rev3)
  Componente4 = NRF24L01
  HC-SR04_Sensor_2 = HC-SR04 Ultrasonic Distance Sensor
  J2 = Piezo Speaker

nets:
  N1: Componente1.IRQ, Componente2.D12/MISO
  N2: Componente1.MOSI, Componente2.D11_PWM/MOSI
  N3: Componente1.CSN, Componente2.D8
  VCC: Componente1.VCC, Componente2.3V3
  N4: Componente1.SCK, Componente2.D13/SCK
  N5: Componente1.CE, Componente2.D9_PWM
  GND: Componente1.GND, Componente2.GND, HC-SR04_Sensor_1.GND, J1.pin1
  N6: Componente2.D2, J1.pin2
  N7: Componente2.D3_PWM, J2.pin2
  N8: Componente2.D5_PWM, HC-SR04_Sensor_1.TRIG
  N9: Componente2.D6_PWM, HC-SR04_Sensor_1.ECHO
  5V: Componente2.5V, HC-SR04_Sensor_1.VCC
  N10: Componente3.D8, Componente4.CSN
  N11: Componente3.D9_PWM, Componente4.CE
  N12: Componente3.D11_PWM/MOSI, Componente4.MOSI
  N13: Componente3.D12/MISO, Componente4.IRQ
  N14: Componente3.D13/SCK, Componente4.SCK
  GND_2: Componente3.GND, Componente4.GND, HC-SR04_Sensor_2.GND
  N15: Componente3.D5_PWM, HC-SR04_Sensor_2.TRIG
  N16: Componente3.D6_PWM, HC-SR04_Sensor_2.ECHO
  3V3: Componente3.3V3, Componente4.VCC
  5V_2: Componente3.5V, HC-SR04_Sensor_2.VCC
